// Logisim project 2bit ALU.circ as structural Verilog: 1 circuit, main circuit main
module main (
  input  A,
  input  B,
  input  in_3,
  input  [2:0] in_4,
  input  in_5,
  input  in_6,
  output out_7,
  output out_8,
  output out_9
);

  wire adder_1_out, and_1_out, nor_1_out, not_1_out, or_1_out, subtractor_1_out, xnor_1_out, xor_1_out;

  and and_1 (and_1_out, A, B);
  or or_1 (or_1_out, A, B);
  xor xor_1 (xor_1_out, A, B);
  nor nor_1 (nor_1_out, A, B);
  Adder #(.width(1)) adder_1 (.a(A), .b(B), .out(adder_1_out), .cin(in_6), .cout(out_9));
  Subtractor #(.width(1)) subtractor_1 (.a(B), .b(A), .out(subtractor_1_out), .bin(in_5), .bout(out_8));
  Multiplexer #(.select(3)) multiplexer_1 (
    .in0(and_1_out), .in1(or_1_out), .in2(xor_1_out), .in3(nor_1_out), .in4(not_1_out), .in5(adder_1_out),
    .in6(subtractor_1_out), .in7(xnor_1_out), .out(out_7), .sel(in_4));  // open: en
  not not_1 (not_1_out, in_3);
  xnor xnor_1 (xnor_1_out, A, B);
endmodule
