// Logisim project D FF.circ as structural Verilog: 1 circuit, main circuit main
module main (
  input  D
);

  wire clock_1_out, nand_1_out, nand_2_out, nand_3_out, nand_4_out, not_1_out;

  not not_1 (not_1_out, D);
  Clock clock_1 (.out(clock_1_out));
  nand nand_1 (nand_1_out, D, clock_1_out);
  nand nand_2 (nand_2_out, clock_1_out, not_1_out);
  nand nand_3 (nand_3_out, nand_1_out, nand_4_out);
  nand nand_4 (nand_4_out, nand_3_out, nand_2_out);
  LED led_1 (.in(nand_3_out));
  LED led_2 (.in(nand_4_out));
endmodule
