// Logisim project Distributive-II(LHS).circ as structural Verilog: 1 circuit, main circuit main
module main (
  input  in_1,
  input  in_2,
  input  in_3,
  output out_4
);

  wire or_1_out;

  or or_1 (or_1_out, in_2, in_3);
  and and_1 (out_4, in_1, or_1_out);
endmodule
