// Logisim project DEMUX.circ as structural Verilog: 1 circuit, main circuit main
module main (
  input  S1,
  input  S0,
  input  D,
  output yo,
  output y1,
  output y2,
  output y3
);

  wire not_1_out, not_2_out;

  not not_1 (not_1_out, S1);
  not not_2 (not_2_out, S0);
  and and_1 (yo, not_1_out, not_2_out, D);
  and and_2 (y1, S1, not_2_out, D);
  and and_3 (y2, not_1_out, S0, D);
  and and_4 (y3, S1, S0, D);
endmodule
